// Logisim project 16bitSingleCycleMIPS.circ as structural Verilog: 4 circuits, main circuit main
module main (
  input  in_1,
  input  in_2,
  input  [15:0] in_3,
  output [3:0] out_4,
  output [15:0] out_5,
  output [15:0] out_6,
  output [15:0] out_7,
  output [15:0] out_8,
  output [15:0] out_9,
  output [15:0] out_10,
  output [3:0] out_11,
  output [3:0] out_12,
  output [31:0] out_13,
  output [15:0] out_14,
  output [3:0] out_15,
  output [3:0] out_16
);

  wire alu_1_zero, and_1_out, CLK, contpro_1_alumux, contpro_1_branch, contpro_1_datatoreg,
       contpro_1_datawrite, contpro_1_jump, contpro_1_regaddress, contpro_1_regwrite, not_1_out;
  wire [15:0] adder_1_out, adder_2_out, controlled_buffer_1_out, multiplexer_1_out, multiplexer_2_out,
       multiplexer_4_out;

  Multiplexer #(.width(16), .enable("false")) multiplexer_1 (
    .in0(adder_1_out), .in1(adder_2_out), .out(multiplexer_1_out), .sel(and_1_out));
  Multiplexer #(.width(16), .enable("false")) multiplexer_2 (
    .in0(multiplexer_1_out), .in1(out_7), .out(multiplexer_2_out), .sel(contpro_1_jump));
  Register #(.width(16)) register_1 (.D(multiplexer_2_out), .en(1'b1), .Q(out_6), .clk(CLK), .clr(in_2));
  Adder #(.width(16)) adder_1 (.a(out_6), .b(in_3), .out(adder_1_out));  // open: cin, cout
  Adder #(.width(16)) adder_2 (.a(adder_1_out), .b(out_7), .out(adder_2_out));  // open: cin, cout
  ROM #(.addrWidth(16), .dataWidth(32)) rom_1 (
    .addr(out_6), .data({out_13[31:25], out_12, out_13[20:16], out_7}), .sel(in_1));
  CONTpro contpro_1 (
    .OPCode(out_13[31:26]), .Funct(out_7[5:0]), .Jump(contpro_1_jump), .DataToReg(contpro_1_datatoreg),
    .DataWrite(contpro_1_datawrite), .Branch(contpro_1_branch), .ALUmux(contpro_1_alumux),
    .RegAddress(contpro_1_regaddress), .RegWrite(contpro_1_regwrite), .out_10(out_4));
  _16RegFile u_16regfile_1 (
    .A1(out_12), .A3(out_11), .A2(out_13[19:16]), .WD3(out_10), .out_7(out_9), .out_8(out_14),
    .in_6(contpro_1_regwrite), .in_5(CLK));
  Clock clock_1 (.out(CLK));
  Multiplexer #(.width(4), .enable("false")) multiplexer_3 (
    .in0(out_13[19:16]), .in1(out_7[14:11]), .out(out_11), .sel(contpro_1_regaddress));
  Multiplexer #(.width(16), .enable("false")) multiplexer_4 (
    .in0(out_14), .in1(out_7), .out(multiplexer_4_out), .sel(contpro_1_alumux));
  ALU alu_1 (
    .Data1(out_9), .Data2(multiplexer_4_out), .out_5(out_5), .Zero(alu_1_zero), .in_2(out_4),
    .Shamp(out_7[9:6]));  // open: out_7
  and and_1 (and_1_out, contpro_1_branch, alu_1_zero);
  Multiplexer #(.width(16), .enable("false")) multiplexer_5 (
    .in0(out_5), .in1(controlled_buffer_1_out), .out(out_10), .sel(contpro_1_datatoreg));
  assign controlled_buffer_1_out = contpro_1_datawrite ? out_14 : 16'bz;  // Controlled_Buffer controlled_buffer_1
  not not_1 (not_1_out, contpro_1_datawrite);
  RAM #(.addrWidth(16), .dataWidth(16)) ram_1 (
    .addr(out_5), .data(controlled_buffer_1_out), .clk(CLK), .ld(not_1_out));  // open: sel, clr

  assign out_8 = out_7;
  assign {out_13[24:21], out_13[15:0]} = {out_12, out_7};
  assign out_15 = out_7[9:6];
  assign out_16 = out_13[19:16];

  // Other names for the same wires on the sheet: A3[3:0] = out_11;
  //   D[31:0] = {out_13[31:25], out_12, out_13[20:16], out_7}; Shamp[3:0] = out_7[9:6]; A2[3:0] = out_13[19:16];
  //   A1[3:0] = out_12; Data[15:0] = out_10; RD1[15:0] = out_9; RD2[15:0] = out_14

  // Notes on the sheet:
  //   jump
  //   Debugging Box
  //   contents of rom_1 (hex, n*v repeats v):
  //   40010020 40020018 20220006 22182a 20600002 411022 8000002 220822 8000002 402f0000 8000000 a0240020
  //   3425f442 53100 53901
  //   FUNC
  //   OP
  //    RegWrite
  //   RegAddress
  //   AluMux
  //   ALUCont
  //   Branch
  //   DataWrite
  //   DataToReg
endmodule

module _16RegFile (
  input  [3:0] A1,
  input  [3:0] A3,
  input  [3:0] A2,
  input  [15:0] WD3,
  input  in_5,
  input  in_6,
  output [15:0] out_7,
  output [15:0] out_8
);

  wire and_1_out, and_2_out, and_3_out, and_4_out, and_5_out, and_6_out, and_7_out, and_8_out, and_9_out,
       and_10_out, and_11_out, and_12_out, and_13_out, and_14_out, and_15_out, and_16_out, decoder_1_out0,
       decoder_1_out1, decoder_1_out2, decoder_1_out3, decoder_1_out4, decoder_1_out5, decoder_1_out6,
       decoder_1_out7, decoder_1_out8, decoder_1_out9, decoder_1_out10, decoder_1_out11, decoder_1_out12,
       decoder_1_out13, decoder_1_out14, decoder_1_out15;
  wire [15:0] register_1_q, register_2_q, register_3_q, register_4_q, register_5_q, register_6_q,
       register_7_q, register_8_q, register_9_q, register_10_q, register_11_q, register_12_q, register_13_q,
       register_14_q, register_15_q, register_16_q;

  Decoder #(.select(4), .enable("false")) decoder_1 (
    .out0(decoder_1_out0), .out1(decoder_1_out1), .out2(decoder_1_out2), .out3(decoder_1_out3),
    .out4(decoder_1_out4), .out5(decoder_1_out5), .out6(decoder_1_out6), .out7(decoder_1_out7),
    .out8(decoder_1_out8), .out9(decoder_1_out9), .out10(decoder_1_out10), .out11(decoder_1_out11),
    .out12(decoder_1_out12), .out13(decoder_1_out13), .out14(decoder_1_out14), .out15(decoder_1_out15),
    .sel(A3));
  and and_1 (and_1_out, decoder_1_out0, in_6);
  and and_2 (and_2_out, decoder_1_out1, in_6);
  and and_3 (and_3_out, decoder_1_out2, in_6);
  and and_4 (and_4_out, decoder_1_out3, in_6);
  and and_5 (and_5_out, decoder_1_out4, in_6);
  and and_6 (and_6_out, decoder_1_out5, in_6);
  and and_7 (and_7_out, decoder_1_out6, in_6);
  and and_8 (and_8_out, decoder_1_out7, in_6);
  Register #(.width(16)) register_1 (.D(WD3), .en(and_1_out), .Q(register_1_q), .clk(in_5));  // open: clr
  Register #(.width(16)) register_2 (.D(WD3), .en(and_2_out), .Q(register_2_q), .clk(in_5));  // open: clr
  Register #(.width(16)) register_3 (.D(WD3), .en(and_3_out), .Q(register_3_q), .clk(in_5));  // open: clr
  Register #(.width(16)) register_4 (.D(WD3), .en(and_4_out), .Q(register_4_q), .clk(in_5));  // open: clr
  Register #(.width(16)) register_5 (.D(WD3), .en(and_5_out), .Q(register_5_q), .clk(in_5));  // open: clr
  Register #(.width(16)) register_6 (.D(WD3), .en(and_6_out), .Q(register_6_q), .clk(in_5));  // open: clr
  Register #(.width(16)) register_7 (.D(WD3), .en(and_7_out), .Q(register_7_q), .clk(in_5));  // open: clr
  Register #(.width(16)) register_8 (.D(WD3), .en(and_8_out), .Q(register_8_q), .clk(in_5));  // open: clr
  and and_9 (and_9_out, decoder_1_out8, in_6);
  and and_10 (and_10_out, decoder_1_out9, in_6);
  and and_11 (and_11_out, decoder_1_out10, in_6);
  and and_12 (and_12_out, decoder_1_out11, in_6);
  and and_13 (and_13_out, decoder_1_out12, in_6);
  and and_14 (and_14_out, decoder_1_out13, in_6);
  and and_15 (and_15_out, decoder_1_out14, in_6);
  and and_16 (and_16_out, decoder_1_out15, in_6);
  Register #(.width(16)) register_9 (.D(WD3), .en(and_9_out), .Q(register_9_q), .clk(in_5));  // open: clr
  Register #(.width(16)) register_10 (.D(WD3), .en(and_10_out), .Q(register_10_q), .clk(in_5));  // open: clr
  Register #(.width(16)) register_11 (.D(WD3), .en(and_11_out), .Q(register_11_q), .clk(in_5));  // open: clr
  Register #(.width(16)) register_12 (.D(WD3), .en(and_12_out), .Q(register_12_q), .clk(in_5));  // open: clr
  Register #(.width(16)) register_13 (.D(WD3), .en(and_13_out), .Q(register_13_q), .clk(in_5));  // open: clr
  Register #(.width(16)) register_14 (.D(WD3), .en(and_14_out), .Q(register_14_q), .clk(in_5));  // open: clr
  Register #(.width(16)) register_15 (.D(WD3), .en(and_15_out), .Q(register_15_q), .clk(in_5));  // open: clr
  Register #(.width(16)) register_16 (.D(WD3), .en(and_16_out), .Q(register_16_q), .clk(in_5));  // open: clr
  Multiplexer #(.select(4), .width(16), .enable("false")) multiplexer_1 (
    .in0(register_1_q), .in1(register_2_q), .in2(register_3_q), .in3(register_4_q), .in4(register_5_q),
    .in5(register_6_q), .in6(register_7_q), .in7(register_8_q), .in8(register_9_q), .in9(register_10_q),
    .in10(register_11_q), .in11(register_12_q), .in12(register_13_q), .in13(register_14_q),
    .in14(register_15_q), .in15(register_16_q), .out(out_7), .sel(A1));
  Multiplexer #(.select(4), .width(16), .enable("false")) multiplexer_2 (
    .in0(register_1_q), .in1(register_2_q), .in2(register_3_q), .in3(register_4_q), .in4(register_5_q),
    .in5(register_6_q), .in6(register_7_q), .in7(register_8_q), .in8(register_9_q), .in9(register_10_q),
    .in10(register_11_q), .in11(register_12_q), .in12(register_13_q), .in13(register_14_q),
    .in14(register_15_q), .in15(register_16_q), .out(out_8), .sel(A2));

  // Other names for the same wires on the sheet: clk = in_5; RegWrite = in_6
endmodule

module ALU (
  input  [15:0] Data1,
  input  [3:0] in_2,
  input  [15:0] Data2,
  input  [3:0] Shamp,
  output [15:0] out_5,
  output Zero,
  output [15:0] out_7
);

  wire comparator_1_lt;
  wire [15:0] adder_1_out, and_1_out, bit_extender_1_out, or_1_out, shifter_2_out, subtractor_1_out;

  Shifter #(.width(16)) shifter_1 (.in(Data2), .\dist (Shamp), .out(out_7));
  Shifter #(.width(16), .shift("lr")) shifter_2 (.in(Data2), .\dist (Shamp), .out(shifter_2_out));
  Adder #(.width(16)) adder_1 (.a(Data1), .b(Data2), .out(adder_1_out));  // open: cin, cout
  Subtractor #(.width(16)) subtractor_1 (.a(Data1), .b(Data2), .out(subtractor_1_out));  // open: bin, bout
  assign or_1_out = Data1 | Data2;  // OR_Gate or_1, 16 bits wide
  assign and_1_out = Data1 & Data2;  // AND_Gate and_1, 16 bits wide
  Comparator #(.width(16)) comparator_1 (.a(Data1), .b(Data2), .eq(Zero), .lt(comparator_1_lt));  // open: gt
  assign bit_extender_1_out = {{15{1'b0}}, comparator_1_lt};  // Bit_Extender bit_extender_1
  Multiplexer #(.select(4), .width(16), .enable("false")) multiplexer_1 (
    .in0(and_1_out), .in1(or_1_out), .in2(adder_1_out), .in6(subtractor_1_out), .in7(bit_extender_1_out),
    .in8(out_7), .in9(shifter_2_out), .out(out_5), .sel(in_2));  // open: in3, in4, in5, in10, in11, in12, in13, in14, in15
endmodule

module CONTpro (
  input  [5:0] OPCode,
  input  [5:0] Funct,
  output Jump,
  output DataToReg,
  output DataWrite,
  output Branch,
  output ALUmux,
  output RegAddress,
  output RegWrite,
  output [3:0] out_10
);

  wire addf_out, and_1_out, and_2_out, and_3_out, and_4_out, and_5_out, and_6_out, and_7_out, and_8_out,
       and_9_out, and_10_out, andf_out, not_3_out, or_1_out, or_2_out, or_3_out, orf_out, sltf_out, subf_out;
  wire [1:0] not_2_out, rom_1_data;
  wire [3:3] rom_1_data_2;
  wire [5:0] not_1_out;

  assign not_1_out = ~Funct;  // NOT_Gate not_1, 6 bits wide
  assign not_2_out = ~rom_1_data;  // NOT_Gate not_2, 2 bits wide
  not not_3 (not_3_out, rom_1_data_2[3]);
  ROM #(.addrWidth(6), .dataWidth(10)) rom_1 (
    .addr(OPCode),
    .data({RegWrite, RegAddress, ALUmux, Branch, DataWrite, DataToReg, rom_1_data_2[3], rom_1_data, Jump}));  // open: sel
  and and_1 (and_1_out, not_2_out[0], rom_1_data[1]);
  and and_2 (and_2_out, not_2_out[0], not_2_out[1], not_3_out);
  and addf (addf_out, not_1_out[0], not_1_out[1], not_1_out[2], not_1_out[3], Funct[5]);
  and subf (subf_out, not_1_out[3], not_1_out[2], Funct[1], not_1_out[0]);
  and andf (andf_out, not_1_out[0], not_1_out[1], not_1_out[3], Funct[2]);
  and orf (orf_out, Funct[0], not_1_out[1], Funct[2], not_1_out[3]);
  and sltf (sltf_out, not_1_out[2], Funct[1], not_1_out[0], Funct[3]);
  and and_3 (and_3_out, and_1_out, addf_out);
  and and_4 (and_4_out, and_1_out, subf_out);
  and and_5 (and_5_out, and_1_out, andf_out);
  and and_6 (and_6_out, and_1_out, orf_out);
  and and_7 (and_7_out, and_1_out, sltf_out);
  and and_8 (and_8_out, not_1_out[4], and_1_out, not_1_out[5], not_1_out[3], not_1_out[2], not_1_out[1], not_1_out[0]);
  and and_9 (and_9_out, and_1_out, not_1_out[4], not_1_out[5], not_1_out[3], not_1_out[2], not_1_out[1], Funct[0]);
  or or_1 (or_1_out, and_3_out, and_2_out);
  and and_10 (and_10_out, not_2_out[1], rom_1_data[0]);
  or or_2 (or_2_out, and_10_out, and_4_out);
  or or_3 (or_3_out, and_6_out, rom_1_data_2[3]);
  or or_4 (out_10[1], or_1_out, out_10[2]);
  or or_5 (out_10[2], or_2_out, and_7_out);
  or or_6 (out_10[3], and_8_out, and_9_out);
  or or_7 (out_10[0], or_3_out, and_9_out, and_7_out);

  // Notes on the sheet:
  //   contents of rom_1 (hex, n*v repeats v):
  //   304 0 1 0 11 0 0 0 42 4*0 288 0 0 280 18*0 290 4*0 286 0 0 a0
  //   ALUOP
  //   add
  //   sub
  //   and
  //   or
  //   slt
  //   sll
  //   srl
endmodule
